# Fritzing sketch Testopsætning (saved by Fritzing 0.9.3b)
breadboards: 1

parts:
  Part1 = Arduino Uno (Rev3) - ICSP
  R1 = Resistor [tolerance=±5% resistance=470k package=THT]
  R2 = Resistor [tolerance=±5% resistance=220 package=THT]
  h206 = mystery part, 4 pins [chip_label=h206]

nets:
  N1: Part1.A0, R1.Pin_1, h206.pin3
  N2: Part1.5V, R2.Pin_1, h206.pin4
  N3: Part1.GND, R1.Pin_0, h206.pin2
  N4: R2.Pin_0, h206.pin1
